# Fritzing sketch Sketch (saved by Fritzing 1.0.6)
breadboards: 1

parts:
  U1 = prefix0000 [part_number=" XIAO ESP32C6"]
  U2 = MAX485 [package=dil08]
  120kΩ = Resistor [tolerance=±5% resistance=220 package="2010 [SMD]"]
  Grove1 = Grove OLED 128x96

nets:
  RESET: U1.connector2
  N1: U1.connector3, U2.RE, U2.DE
  N2: U1.connector6, U2.RO
  N3: U1.connector7, U2.DI
  GND: U1.connector12, U2.GND, Grove1.GND
  VCC: U1.connector13, U2.VCC, Grove1.VCC
  N4: U2.A, 120kΩ.Pin_0
  A/B: U2.B, 120kΩ.Pin_1
